# Fritzing sketch NEW SCHEMATIC (saved by Fritzing 0.9.2b)
breadboards: 1

parts:
  Part1 = Arduino Mega 2560 (Rev3)
  LED4 = LED - 5mm [color="Red (633nm)" package="5 mm [THT]"]
  R24 = Resistor [tolerance=±5% resistance=220 package=THT]  # not connected
  R25 = Resistor [tolerance=±5% resistance=100 package=THT]
  LDR3 = PHOTOCELL [package=photocell]  # not connected
  R26 = Resistor [tolerance=±5% resistance=1k package=THT]
  R27 = Resistor [tolerance=±5% resistance=1k package=THT]  # not connected
  R28 = Resistor [tolerance=±5% resistance=8k package=THT]
  C5 = Electrolytic Capacitor [capacitance=10µF package="100 mil [THT, electrolytic]"]
  C6 = Electrolytic Capacitor [capacitance=10µF package="100 mil [THT, electrolytic]"]
  R29 = Resistor [tolerance=±5% resistance=100k package=THT]
  R30 = Resistor [tolerance=±5% resistance=1M package=THT]
  R31 = Resistor [tolerance=±5% resistance=750k package=THT]
  R32 = Resistor [tolerance=±5% resistance=750k package=THT]
  LM360 = Dual Op-Amp [package=so08]
  LED5 = LED - 5mm [color="Red (633nm)" package="5 mm [THT]"]
  R33 = Resistor [tolerance=±5% resistance=220 package=THT]  # not connected
  R34 = Resistor [tolerance=±5% resistance=100 package=THT]
  LDR4 = PHOTOCELL [package=photocell]  # not connected
  R35 = Resistor [tolerance=±5% resistance=1k package=THT]
  R36 = Resistor [tolerance=±5% resistance=1k package=THT]  # not connected
  R37 = Resistor [tolerance=±5% resistance=8k package=THT]
  C7 = Electrolytic Capacitor [capacitance=10µF package="100 mil [THT, electrolytic]"]
  C8 = Electrolytic Capacitor [capacitance=10µF package="100 mil [THT, electrolytic]"]
  R38 = Resistor [tolerance=±5% resistance=100k package=THT]
  R39 = Resistor [tolerance=±5% resistance=1M package=THT]
  S6 = Pushbutton [package="[THT]"]
  S7 = Pushbutton [package="[THT]"]
  R40 = Resistor [tolerance=±5% resistance=10k package=THT]
  S8 = Pushbutton [package="[THT]"]
  R41 = Resistor [tolerance=±5% resistance=10k package=THT]
  S9 = Pushbutton [package="[THT]"]
  R42 = Resistor [tolerance=±5% resistance=10k package=THT]
  7_Segment8 = 7 Segment Display
  7_Segment9 = 7 Segment Display
  7_Segment10 = 7 Segment Display
  R43 = Resistor [tolerance=±5% resistance=220 package=THT]
  R44 = Resistor [tolerance=±5% resistance=220 package=THT]
  R45 = Resistor [tolerance=±5% resistance=220 package=THT]
  R46 = Resistor [tolerance=±5% resistance=220 package=THT]
  7_Segment11 = 7 Segment Display
  LED8 = LED - 5mm [color="Red (633nm)" package="5 mm [THT]"]
  LED9 = LED - 5mm [color="Red (633nm)" package="5 mm [THT]"]
  LED10 = LED - 5mm [color="Red (633nm)" package="5 mm [THT]"]
  LED11 = LED - 5mm [color="Red (633nm)" package="5 mm [THT]"]
  LED12 = LED - 5mm [color="Red (633nm)" package="5 mm [THT]"]
  LED13 = LED - 5mm [color="Red (633nm)" package="5 mm [THT]"]
  LED14 = LED - 5mm [color="Red (633nm)" package="5 mm [THT]"]
  R47 = Resistor [tolerance=±5% resistance=330 package=THT]
  R48 = Resistor [tolerance=±5% resistance=330 package=THT]
  R49 = Resistor [tolerance=±5% resistance=330 package=THT]
  R50 = Resistor [tolerance=±5% resistance=330 package=THT]
  R51 = Resistor [tolerance=±5% resistance=330 package=THT]
  R52 = Resistor [tolerance=±5% resistance=330 package=THT]
  R53 = Resistor [tolerance=±5% resistance=330 package=THT]
  SG2 = Buzzer 12mm [package=buzzer-ccv-kit]
  U3 = BUTTONPAD-4X4 [package=buttonpad-4x4-special]
  Q5 = NPN-Transistor [part_number=SL100 package="TO92 [THT]"]
  Q6 = NPN-Transistor [part_number=SL100 package="TO92 [THT]"]
  Q7 = NPN-Transistor [package="TO92 [THT]"]
  Q8 = NPN-Transistor [package="TO92 [THT]"]
  R54 = Resistor [tolerance=±5% resistance=47k package=THT]
  R55 = Resistor [tolerance=±5% resistance=47k package=THT]
  R56 = Resistor [tolerance=±5% resistance=220 package=THT]
  R57 = Resistor [tolerance=±5% resistance=220 package=THT]
  D3 = Zener Diode [part_number=1N4732A breakdown_voltage=4.5V package="300 mil [THT]"]
  D4 = Zener Diode [part_number=1N4732A breakdown_voltage=5V package="300 mil [THT]"]
  R58 = Resistor [tolerance=±5% resistance=10k package=THT]  # not connected
  R59 = Resistor [tolerance=±5% resistance=10k package=THT]  # not connected
  LED15 = LED - 5mm [color="Red (633nm)" package="5 mm [THT]"]  # not connected
  LED16 = LED - 5mm [color="Green (570nm)" package="5 mm [THT]"]  # not connected
  LED17 = LED - 5mm [color="Red (633nm)" package="5 mm [THT]"]  # not connected
  R60 = Resistor [tolerance=±5% resistance=330 package=THT]
  R61 = Resistor [tolerance=±5% resistance=330 package=THT]
  R62 = Resistor [tolerance=±5% resistance=330 package=THT]
  V15 = DC Power [voltage=6V]

nets:
  N1: Part1.A0, C5.+, R29.Pin_0
  N2: Part1.A1, C7.+, R38.Pin_0
  N3: Part1.A2, D3.cathode, D4.cathode, V15.V+
  N4: Part1.D12_PWM, R46.Pin_1
  N5: Part1.D11_PWM, R45.Pin_1
  N6: Part1.D10_PWM, R44.Pin_1
  N7: Part1.D9_PWM, R43.Pin_1
  N8: Part1.RESET, S6.Pin_3, S6.Pin_4
  5V: Part1.VIN, LED4.anode, LM360.A_V+, LED5.anode, S7.Pin_1, S7.Pin_2, S8.Pin_1, S8.Pin_2, S9.Pin_1, S9.Pin_2
  N9: Part1.D2_PWM, LM360.A_OUT
  N10: Part1.D22, 7_Segment8.Segment_A, 7_Segment9.Segment_A, 7_Segment10.Segment_A, 7_Segment11.Segment_B
  N11: Part1.D23, 7_Segment8.Segment_B, 7_Segment9.Segment_B, 7_Segment10.Segment_B, 7_Segment11.Segment_A
  N12: Part1.D24, 7_Segment8.Segment_C, 7_Segment9.Segment_C, 7_Segment10.Segment_C, 7_Segment11.Segment_C
  N13: Part1.D25, 7_Segment8.Segment_D, 7_Segment9.Segment_D, 7_Segment10.Segment_D, 7_Segment11.Segment_D
  N14: Part1.D26, 7_Segment8.Segment_E, 7_Segment9.Segment_E, 7_Segment10.Segment_E, 7_Segment11.Segment_E
  N15: Part1.D27, 7_Segment8.Segment_F, 7_Segment9.Segment_F, 7_Segment10.Segment_F, 7_Segment11.Segment_F
  N16: Part1.D28, 7_Segment8.Segment_G, 7_Segment9.Segment_G, 7_Segment10.Segment_G, 7_Segment11.Segment_G
  N17: Part1.D29, 7_Segment8.Segment_DP, 7_Segment9.Segment_DP, 7_Segment10.Segment_DP, 7_Segment11.Segment_DP
  N18: Part1.D30, LED13.anode
  N19: Part1.D31, LED11.anode
  N20: Part1.D32, LED8.anode
  N21: Part1.D33, LED12.anode
  N22: Part1.D34, LED10.anode
  N23: Part1.D35, LED14.anode
  N24: Part1.D36, LED9.anode
  N25: Part1.D38, U3.G$3_GND, U3.G$7_GND, U3.G$11_GND, U3.G$15_GND
  N26: Part1.D39, U3.G$2_GND, U3.G$6_GND, U3.G$10_GND, U3.G$14_GND
  N27: Part1.D40, U3.G$1_GND, U3.G$5_GND, U3.G$9_GND, U3.G$13_GND
  N28: Part1.D41, U3.G$0_GND, U3.G$4_GND, U3.G$8_GND, U3.G$12_GND
  N29: Part1.D42, U3.G$3_SIG2
  N30: Part1.D43, U3.G$2_SIG2, U3.G$3_SIG1
  N31: Part1.D44, U3.G$1_SIG2, U3.G$2_SIG1
  N32: Part1.D45, U3.G$0_SIG2, U3.G$1_SIG1
  N33: Part1.D46, SG2.1
  N34: Part1.D47, S7.Pin_3, S7.Pin_4, R40.Pin_0
  N35: Part1.D48, S8.Pin_3, S8.Pin_4, R41.Pin_0
  N36: Part1.D49, S9.Pin_3, S9.Pin_4, R42.Pin_0
  GND: R25.Pin_1, C5.-, C6.-, R30.Pin_1, LM360.A_V-, R34.Pin_1, C7.-, C8.-, R39.Pin_1, S6.Pin_1, S6.Pin_2, R47.Pin_0, R48.Pin_0, R49.Pin_0, R50.Pin_0, R51.Pin_0, R52.Pin_0, R53.Pin_0, SG2.2
  N37: R26.Pin_0, R28.Pin_0, R31.Pin_0
  N38: R29.Pin_1, R30.Pin_0, R32.Pin_0
  N39: R35.Pin_0, R37.Pin_0
  N40: R38.Pin_1, R39.Pin_0
  N41: U3.G$4_SIG2, U3.G$5_SIG1
  N42: U3.G$5_SIG2, U3.G$6_SIG1
  N43: U3.G$6_SIG2, U3.G$7_SIG1
  N44: U3.G$8_SIG2, U3.G$9_SIG1
  N45: U3.G$9_SIG2, U3.G$10_SIG1
  N46: U3.G$10_SIG2, U3.G$11_SIG1
  N47: U3.G$12_SIG2, U3.G$13_SIG1
  N48: U3.G$13_SIG2, U3.G$14_SIG1
  N49: U3.G$14_SIG2, U3.G$15_SIG1
  N50: Q5.C, R56.Pin_0
  N51: Q6.E, Q8.C
  N52: Q7.C, R57.Pin_0
  N53: R54.Pin_0, D3.anode
  N54: R55.Pin_0, D4.anode
  N55: R60.Pin_0, R61.Pin_0, R62.Pin_0
