# Fritzing sketch circuit diagram fritzing (saved by Fritzing 0.9.2b)

parts:
  LED1 = LED - 5mm [color="Red (633nm)" package="5 mm [THT]"]
  R1 = Resistor [tolerance=±5% resistance=220 package=THT]  # not connected
  R2 = Resistor [tolerance=±5% resistance=100 package=THT]
  LDR = PHOTOCELL [package=photocell]  # not connected
  R4 = Resistor [tolerance=±5% resistance=1k package=THT]  # not connected
  R5 = Resistor [tolerance=±5% resistance=1k package=THT]
  R6 = Resistor [tolerance=±5% resistance=8k package=THT]
  C1 = Electrolytic Capacitor [capacitance=10µF package="100 mil [THT, electrolytic]"]
  C2 = Electrolytic Capacitor [capacitance=10µF package="100 mil [THT, electrolytic]"]
  R7 = Resistor [tolerance=±5% resistance=100k package=THT]
  R8 = Resistor [tolerance=±5% resistance=1M package=THT]
  R9 = Resistor [tolerance=±5% resistance=750k package=THT]
  R10 = Resistor [tolerance=±5% resistance=750k package=THT]  # not connected
  LM358 = Dual Op-Amp [package=so08]
  Microcontroller = Arduino Uno (Rev3)
  7_Segment1 = 7 Segment Display
  7_Segment2 = 7 Segment Display
  7_Segment3 = 7 Segment Display
  R14 = Resistor [tolerance=±5% resistance=330 package=THT]
  R15 = Resistor [tolerance=±5% resistance=330 package=THT]
  R16 = Resistor [tolerance=±5% resistance=330 package=THT]

nets:
  5V: LED1.anode, LM358.A_V+
  GND: R2.Pin_1, C1.-, C2.-, R8.Pin_1, LM358.A_V-
  N1: R5.Pin_0, R6.Pin_0
  N2: C1.+, R7.Pin_0
  N3: R7.Pin_1, R8.Pin_0, R9.Pin_0
  N4: LM358.A_OUT, Microcontroller.D2
  N5: Microcontroller.D8, 7_Segment1.Segment_G, 7_Segment2.Segment_G, 7_Segment3.Segment_G
  N6: Microcontroller.D9_PWM, R14.Pin_1
  N7: Microcontroller.D10_PWM/SS, R15.Pin_1
  N8: Microcontroller.D11_PWM/MOSI, R16.Pin_1
  N9: Microcontroller.D0/RX, 7_Segment1.Segment_A, 7_Segment2.Segment_A, 7_Segment3.Segment_A
  N10: Microcontroller.D1/TX, 7_Segment1.Segment_B, 7_Segment2.Segment_B, 7_Segment3.Segment_B
  N11: Microcontroller.D4, 7_Segment1.Segment_C, 7_Segment2.Segment_C, 7_Segment3.Segment_C
  N12: Microcontroller.D5_PWM, 7_Segment1.Segment_D, 7_Segment2.Segment_D, 7_Segment3.Segment_D
  N13: Microcontroller.D6_PWM, 7_Segment1.Segment_E, 7_Segment2.Segment_E, 7_Segment3.Segment_E
  N14: Microcontroller.D7, 7_Segment1.Segment_F, 7_Segment2.Segment_F, 7_Segment3.Segment_F
  N15: 7_Segment1.Segment_DP, 7_Segment2.Segment_DP, 7_Segment3.Segment_DP
