# Fritzing sketch schematic draft 1 (saved by Fritzing 0.9.2b)
breadboards: 1

parts:
  Part1 = Arduino Mega 2560 (Rev3)
  LED4 = LED - 5mm [color="Red (633nm)" package="5 mm [THT]"]
  R24 = Resistor [tolerance=±5% resistance=220 package=THT]  # not connected
  R25 = Resistor [tolerance=±5% resistance=100 package=THT]
  LDR3 = PHOTOCELL [package=photocell]  # not connected
  R26 = Resistor [tolerance=±5% resistance=1k package=THT]
  R27 = Resistor [tolerance=±5% resistance=1k package=THT]  # not connected
  R28 = Resistor [tolerance=±5% resistance=8k package=THT]
  C5 = Electrolytic Capacitor [capacitance=10µF package="100 mil [THT, electrolytic]"]
  C6 = Electrolytic Capacitor [capacitance=10µF package="100 mil [THT, electrolytic]"]
  R29 = Resistor [tolerance=±5% resistance=100k package=THT]
  R30 = Resistor [tolerance=±5% resistance=1M package=THT]
  R31 = Resistor [tolerance=±5% resistance=750k package=THT]
  R32 = Resistor [tolerance=±5% resistance=750k package=THT]
  LM360 = Dual Op-Amp [package=so08]
  LED5 = LED - 5mm [color="Red (633nm)" package="5 mm [THT]"]
  R33 = Resistor [tolerance=±5% resistance=220 package=THT]  # not connected
  R34 = Resistor [tolerance=±5% resistance=100 package=THT]
  LDR4 = PHOTOCELL [package=photocell]  # not connected
  R35 = Resistor [tolerance=±5% resistance=1k package=THT]
  R36 = Resistor [tolerance=±5% resistance=1k package=THT]  # not connected
  R37 = Resistor [tolerance=±5% resistance=8k package=THT]
  C7 = Electrolytic Capacitor [capacitance=10µF package="100 mil [THT, electrolytic]"]
  C8 = Electrolytic Capacitor [capacitance=10µF package="100 mil [THT, electrolytic]"]
  R38 = Resistor [tolerance=±5% resistance=100k package=THT]
  R39 = Resistor [tolerance=±5% resistance=1M package=THT]
  S6 = Pushbutton [package="[THT]"]
  S7 = Pushbutton [package="[THT]"]
  R40 = Resistor [tolerance=±5% resistance=10k package=THT]
  S8 = Pushbutton [package="[THT]"]
  R41 = Resistor [tolerance=±5% resistance=10k package=THT]
  S9 = Pushbutton [package="[THT]"]
  R42 = Resistor [tolerance=±5% resistance=10k package=THT]
  7_Segment8 = 7 Segment Display
  7_Segment9 = 7 Segment Display
  7_Segment10 = 7 Segment Display
  R43 = Resistor [tolerance=±5% resistance=220 package=THT]
  R44 = Resistor [tolerance=±5% resistance=220 package=THT]
  R45 = Resistor [tolerance=±5% resistance=220 package=THT]
  R46 = Resistor [tolerance=±5% resistance=220 package=THT]
  7_Segment11 = 7 Segment Display
  LED8 = LED - 5mm [color="Red (633nm)" package="5 mm [THT]"]
  LED9 = LED - 5mm [color="Red (633nm)" package="5 mm [THT]"]
  LED10 = LED - 5mm [color="Red (633nm)" package="5 mm [THT]"]
  LED11 = LED - 5mm [color="Red (633nm)" package="5 mm [THT]"]
  LED12 = LED - 5mm [color="Red (633nm)" package="5 mm [THT]"]
  LED13 = LED - 5mm [color="Red (633nm)" package="5 mm [THT]"]
  LED14 = LED - 5mm [color="Red (633nm)" package="5 mm [THT]"]
  R47 = Resistor [tolerance=±5% resistance=330 package=THT]
  R48 = Resistor [tolerance=±5% resistance=330 package=THT]
  R49 = Resistor [tolerance=±5% resistance=330 package=THT]
  R50 = Resistor [tolerance=±5% resistance=330 package=THT]
  R51 = Resistor [tolerance=±5% resistance=330 package=THT]
  R52 = Resistor [tolerance=±5% resistance=330 package=THT]
  R53 = Resistor [tolerance=±5% resistance=330 package=THT]
  SG2 = Buzzer 12mm [package=buzzer-ccv-kit]

nets:
  N1: Part1.A0, C5.+, R29.Pin_0
  N2: Part1.A1, C7.+, R38.Pin_0
  N3: Part1.D12_PWM, R46.Pin_1
  N4: Part1.D11_PWM, R45.Pin_1
  N5: Part1.D10_PWM, R44.Pin_1
  N6: Part1.D9_PWM, R43.Pin_1
  N7: Part1.RESET, S6.Pin_3, S6.Pin_4
  N8: Part1.D2_PWM, LM360.A_OUT
  N9: Part1.D22, 7_Segment8.Segment_A, 7_Segment9.Segment_A, 7_Segment10.Segment_A, 7_Segment11.Segment_B
  N10: Part1.D23, 7_Segment8.Segment_B, 7_Segment9.Segment_B, 7_Segment10.Segment_B, 7_Segment11.Segment_A
  N11: Part1.D24, 7_Segment8.Segment_C, 7_Segment9.Segment_C, 7_Segment10.Segment_C, 7_Segment11.Segment_C
  N12: Part1.D25, 7_Segment8.Segment_D, 7_Segment9.Segment_D, 7_Segment10.Segment_D, 7_Segment11.Segment_D
  N13: Part1.D26, 7_Segment8.Segment_E, 7_Segment9.Segment_E, 7_Segment10.Segment_E, 7_Segment11.Segment_E
  N14: Part1.D27, 7_Segment8.Segment_F, 7_Segment9.Segment_F, 7_Segment10.Segment_F, 7_Segment11.Segment_F
  N15: Part1.D28, 7_Segment8.Segment_G, 7_Segment9.Segment_G, 7_Segment10.Segment_G, 7_Segment11.Segment_G
  N16: Part1.D29, 7_Segment8.Segment_DP, 7_Segment9.Segment_DP, 7_Segment10.Segment_DP, 7_Segment11.Segment_DP
  N17: Part1.D30, LED13.anode
  N18: Part1.D31, LED11.anode
  N19: Part1.D32, LED8.anode
  N20: Part1.D33, LED12.anode
  N21: Part1.D34, LED10.anode
  N22: Part1.D35, LED14.anode
  N23: Part1.D36, LED9.anode
  N24: Part1.D46, SG2.1
  N25: Part1.D47, S7.Pin_3, S7.Pin_4, R40.Pin_0
  N26: Part1.D48, S8.Pin_3, S8.Pin_4, R41.Pin_0
  N27: Part1.D49, S9.Pin_3, S9.Pin_4, R42.Pin_0
  5V: LED4.anode, LM360.A_V+, LED5.anode, S7.Pin_1, S7.Pin_2, S8.Pin_1, S8.Pin_2, S9.Pin_1, S9.Pin_2
  GND: R25.Pin_1, C5.-, C6.-, R30.Pin_1, LM360.A_V-, R34.Pin_1, C7.-, C8.-, R39.Pin_1, S6.Pin_1, S6.Pin_2, R47.Pin_0, R48.Pin_0, R49.Pin_0, R50.Pin_0, R51.Pin_0, R52.Pin_0, R53.Pin_0, SG2.2
  N28: R26.Pin_0, R28.Pin_0, R31.Pin_0
  N29: R29.Pin_1, R30.Pin_0, R32.Pin_0
  N30: R35.Pin_0, R37.Pin_0
  N31: R38.Pin_1, R39.Pin_0
